# Fritzing sketch tugas week 5 (saved by Fritzing 0.9.3b)
breadboards: 1

parts:
  Raspberry_Pi_1 = Raspberry Pi 3 [part_number=RPI-3-V1.2]
  Sensor_Gas_MQ2 = GAS_SENSOR [package=mq-3]
  R1 = Resistor [tolerance=±5% resistance=220 package="2010 [SMD]"]
  LED1 = LED - 3mm [color="Red (633nm)" package="3 mm [THT]"]

nets:
  N1: Raspberry_Pi_1.GND, Sensor_Gas_MQ2.A1, R1.Pin_1, LED1.cathode, LED1.anode
  N2: Raspberry_Pi_1.GIPO21, R1.Pin_0
  N3: Raspberry_Pi_1.5V, Sensor_Gas_MQ2.B1
